# Fritzing sketch BRPT_v1 (saved by Fritzing 0.9.9b)
circuit board: 8cm x 6cm
breadboards: 1

parts:
  Teensy_4_0 = Teensy 3.1
  CR2032 = Adafruit 20mm Coin Cell Breakout Board [part_number="Adafruit #1870"]
  U1 = Voltage Regulator - 5V [package="TO220 [THT]"]
  Gnd_Gnd_Bat_?_TX_Gnd_ST = female pin header, 7 pins [form="♀ (female)"]
  5V_Gnd_3V3_SH_RX_Gnd_PDI = female pin header, 7 pins [form="♀ (female)"]
  Gnd_SDA_SCL_3V3 = female pin header, 4 pins [form="♀ (female)"]
  Gnd_SDA_SCL_3V3_2 = female pin header, 4 pins [form="♀ (female)"]
  +_- = female pin header, 2 pins [form="♀ (female)"]
  10k = Resistor [tolerance=±5% resistance=10k power=0.25 package=THT]
  10k_2 = Resistor [tolerance=±5% resistance=10k power=0.25 package=THT]
  TX_RX = female pin header, 2 pins [form="♀ (female)"]
  TX_RX_2 = female pin header, 2 pins [form="♀ (female)"]
  J1 = female pin header, 4 pins [form="♀ (female)"]

nets:
  GND: Teensy_4_0.GND, CR2032.GND, 5V_Gnd_3V3_SH_RX_Gnd_PDI.pin1, 5V_Gnd_3V3_SH_RX_Gnd_PDI.pin2, Gnd_SDA_SCL_3V3.pin4, Gnd_SDA_SCL_3V3_2.pin4, J1.pin1
  N1: Teensy_4_0.D0, TX_RX_2.pin2
  N2: Teensy_4_0.D1, TX_RX_2.pin1
  N3: Teensy_4_0.A4/D18, Gnd_SDA_SCL_3V3.pin3, Gnd_SDA_SCL_3V3_2.pin3, 10k.Pin_0
  N4: Teensy_4_0.A5/D19, Gnd_SDA_SCL_3V3.pin2, Gnd_SDA_SCL_3V3_2.pin2, 10k_2.Pin_0
  N5: Teensy_4_0.3V3, Gnd_SDA_SCL_3V3.pin1, Gnd_SDA_SCL_3V3_2.pin1, 10k.Pin_1, 10k_2.Pin_1
  N6: Teensy_4_0.Vin, U1.output_voltage, 5V_Gnd_3V3_SH_RX_Gnd_PDI.pin7
  N7: CR2032.V+, Gnd_Gnd_Bat_?_TX_Gnd_ST.pin3
  N8: U1.input_voltage, +_-.pin1
  N9: U1.GND, Gnd_Gnd_Bat_?_TX_Gnd_ST.pin2, +_-.pin2
  N10: Gnd_Gnd_Bat_?_TX_Gnd_ST.pin5, TX_RX.pin2
  N11: 5V_Gnd_3V3_SH_RX_Gnd_PDI.pin3, TX_RX.pin1
  N12: 5V_Gnd_3V3_SH_RX_Gnd_PDI.pin4, J1.pin4

custom parts:
  Adafruit 20mm Coin Cell Breakout Board: Simple but effective - this sewable breakout board has a CR2032 coin cell battery holder soldered on and 0.1" pitch breakout pins for easy connecting. Great for powering very low-current projects, or adding a battery backup circuit to a real-time-clock or similar.
